// Logisim project Circuito_Generate_Key_stream.circ as structural Verilog: 10 circuits, main circuit Bloco_Dados
// Bloco de Dados
module Bloco_Dados (
  input  clock,
  input  reset,
  input  [7:0] data,
  input  init,
  input  rst_ijk,
  input  wrI,
  input  Mux1,
  input  wrJ,
  input  [1:0] Mux2,
  input  wrK,
  input  [7:0] data_in,
  input  [1:0] Mux3,
  input  MuxData,
  input  MuxAux,
  input  wrAux,
  input  [1:0] Mux4,
  input  rst_aux,
  output [7:0] A,
  output [7:0] data_out,
  output aux_four,
  output TextSize_gt
);

  wire and_1_out, or_1_out, or_2_out;
  wire [6:0] adder_1_out;
  wire [7:0] divider_1_rem, multiplexer_1_out, multiplexer_2_out, multiplexer_3_out, multiplexer_4_out,
       multiplexer_5_out, not_1_out, RegAux_q, RegI_q, RegJ_q, RegK_q, RegKeyStream_q, RegState_q,
       RegStateSize_q, RegTextSize_q;

  Multiplexer #(.width(8), .enable("false")) multiplexer_1 (
    .in0(data_in), .in1({TextSize_gt, adder_1_out}), .out(multiplexer_1_out), .sel(MuxAux));
  Register RegI (.D(divider_1_rem), .en(wrI), .Q(RegI_q), .clk(clock), .clr(or_1_out));
  or or_1 (or_1_out, rst_ijk, reset);
  Register RegJ (.D(divider_1_rem), .en(wrJ), .Q(RegJ_q), .clk(clock), .clr(or_1_out));
  Register RegK (.D({TextSize_gt, adder_1_out}), .en(wrK), .Q(RegK_q), .clk(clock), .clr(or_1_out));
  Register RegAux (.D(multiplexer_1_out), .en(wrAux), .Q(RegAux_q), .clk(clock), .clr(or_2_out));
  or or_2 (or_2_out, reset, rst_aux);
  Register RegKeyStream (.D(data), .en(init), .Q(RegKeyStream_q), .clk(clock), .clr(reset));
  Register RegTextSize (.D(RegKeyStream_q), .en(init), .Q(RegTextSize_q), .clk(clock), .clr(reset));
  assign not_1_out = ~RegTextSize_q;  // NOT_Gate not_1, 8 bits wide
  Register RegStateSize (.D(RegTextSize_q), .en(init), .Q(RegStateSize_q), .clk(clock), .clr(reset));
  Multiplexer #(.select(2), .width(8), .enable("false")) multiplexer_2 (
    .in0(RegK_q), .in1(RegJ_q), .in2(RegI_q), .in3(RegAux_q), .out(multiplexer_2_out), .sel(Mux3));
  Multiplexer #(.select(2), .width(8), .enable("false")) multiplexer_3 (
    .in0(not_1_out), .in1(8'h1), .in2(data_in), .in3({8{1'b0}}), .out(multiplexer_3_out), .sel(Mux4));
  and and_1 (and_1_out, ~Mux4[0], ~Mux4[1]);  // AND_Gate
  Register RegState (.D(RegStateSize_q), .en(init), .Q(RegState_q), .clk(clock), .clr(reset));
  Adder adder_1 (
    .a(multiplexer_2_out), .b(multiplexer_3_out), .out({TextSize_gt, adder_1_out}), .cin(and_1_out));  // open: cout
  Divider divider_1 (.a({TextSize_gt, adder_1_out}), .b(RegStateSize_q), .rem(divider_1_rem));  // open: out, upper
  Multiplexer #(.width(8), .enable("false")) multiplexer_4 (
    .in0(RegState_q), .in1(RegKeyStream_q), .out(multiplexer_4_out), .sel(Mux1));
  Multiplexer #(.select(2), .width(8), .enable("false")) multiplexer_5 (
    .in0(RegJ_q), .in1(RegK_q), .in2(RegI_q), .in3(divider_1_rem), .out(multiplexer_5_out), .sel(Mux2));
  Adder adder_2 (.a(multiplexer_4_out), .b(multiplexer_5_out), .out(A));  // open: cin, cout
  Multiplexer #(.width(8), .enable("false")) multiplexer_6 (
    .in0(data_in), .in1(RegAux_q), .out(data_out), .sel(MuxData));
  and and_2 (aux_four, ~RegAux_q[0], ~RegAux_q[1], RegAux_q[2], ~RegAux_q[3], ~RegAux_q[4], ~RegAux_q[5], ~RegAux_q[6], ~RegAux_q[7]);  // AND_Gate

  // Other names for the same wires on the sheet: clk = clock; rst = reset
endmodule

module main (
  input  [7:0] data,
  output done
);

  wire button_sinc_1_bt_out, clk, data_av_out, generate_key_stream_1_ld, generate_key_stream_1_sel,
       not_1_out, rst;
  wire [2:0] generate_key_stream_1_current_state;
  wire [7:0] generate_key_stream_1_a, generate_key_stream_1_data_out, ram_1_data, RegMEM_q;

  Clock clock (.out(clk));
  Button reset (.out(rst));
  Button data_av (.out(data_av_out));
  // Probe on data
  // Probe on data
  button_sinc button_sinc_1 (.bt_in(data_av_out), .clock(clk), .reset(rst), .bt_out(button_sinc_1_bt_out));
  // Probe on generate_key_stream_1_current_state
  Generate_Key_Stream generate_key_stream_1 (
    .clk(clk), .rst(rst), .data_av(button_sinc_1_bt_out), .data(data), .done(done),
    .A(generate_key_stream_1_a), .data_in(RegMEM_q), .data_out(generate_key_stream_1_data_out),
    .sel(generate_key_stream_1_sel), .ld(generate_key_stream_1_ld),
    .Current_State(generate_key_stream_1_current_state));
  not not_1 (not_1_out, generate_key_stream_1_ld);
  RAM ram_1 (
    .addr(generate_key_stream_1_a), .data(ram_1_data), .sel(generate_key_stream_1_sel), .clk(clk),
    .ld(generate_key_stream_1_ld));  // open: clr
  assign ram_1_data = not_1_out ? generate_key_stream_1_data_out : 8'bz;  // Controlled_Buffer controlled_buffer_1
  Register RegMEM (.D(ram_1_data), .en(generate_key_stream_1_ld), .Q(RegMEM_q), .clk(clk), .clr(rst));
endmodule

// Bloco de Controle
module Bloco_Controle (
  input  data_av,
  input  aux_four,
  input  text_gt,
  input  rst,
  input  clk,
  output init,
  output wrAux,
  output res_aux,
  output done,
  output Mux1,
  output [1:0] Mux2,
  output [1:0] Mux3,
  output [1:0] Mux4,
  output MuxAux,
  output wrI,
  output wrJ,
  output MuxData,
  output wrK,
  output rst_IJK,
  output sel,
  output [2:0] current_state,
  output ld
);

  wire prox_estado_1_p0, prox_estado_1_p1, prox_estado_1_p2;

  prox_estado prox_estado_1 (
    .Q2(current_state[2]), .Q1(current_state[1]), .Q0(current_state[0]), .data_av(data_av),
    .k_four(aux_four), .text_gt(text_gt), .P2(prox_estado_1_p2), .P1(prox_estado_1_p1), .P0(prox_estado_1_p0));
  D_Flip_Flop d_ff_1 (
    .clk(clk), .D(prox_estado_1_p2), .Q(current_state[2]), .en(1'b1), .reset(rst));  // open: Qn, preset
  D_Flip_Flop d_ff_2 (
    .clk(clk), .D(prox_estado_1_p1), .Q(current_state[1]), .en(1'b1), .reset(rst));  // open: Qn, preset
  D_Flip_Flop d_ff_3 (
    .clk(clk), .D(prox_estado_1_p0), .Q(current_state[0]), .en(1'b1), .reset(rst));  // open: Qn, preset
  saidas_mealy saidas_mealy_1 (
    .Q2(current_state[2]), .Q1(current_state[1]), .Q0(current_state[0]), .data_av(data_av),
    .aux_four(aux_four), .text_gt(text_gt), .init(init), .wrAux(wrAux), .res_aux(res_aux), .done(done));
  saidas_moore_2 saidas_moore_2_1 (
    .Q2(current_state[2]), .Q1(current_state[1]), .Q0(current_state[0]), .rst_IJK(rst_IJK), .sel(sel), .ld(ld));
  saidas_moore saidas_moore_1 (
    .Q2(current_state[2]), .Q1(current_state[1]), .Q0(current_state[0]), .Mux1(Mux1), .Mux2_1(Mux2[1]),
    .Mux2_0(Mux2[0]), .Mux3_1(Mux3[1]), .Mux3_0(Mux3[0]), .Mux4_1(Mux4[1]), .Mux4_0(Mux4[0]),
    .MuxAux(MuxAux), .wrI(wrI), .wrJ(wrJ), .MuxData(MuxData), .wrK(wrK));
endmodule

// Processor
module Generate_Key_Stream (
  input  [7:0] data_in,
  input  clk,
  input  rst,
  input  data_av,
  input  [7:0] data,
  output done,
  output [7:0] A,
  output [7:0] data_out,
  output sel,
  output ld,
  output [2:0] Current_State
);

  wire bloco_controle_1_init, bloco_controle_1_mux1, bloco_controle_1_muxaux, bloco_controle_1_muxdata,
       bloco_controle_1_res_aux, bloco_controle_1_rst_ijk, bloco_controle_1_wraux, bloco_controle_1_wri,
       bloco_controle_1_wrj, bloco_controle_1_wrk, bloco_dados_1_aux_four, bloco_dados_1_textsize_gt;
  wire [1:0] bloco_controle_1_mux2, bloco_controle_1_mux3, bloco_controle_1_mux4;

  Bloco_Controle bloco_controle_1 (
    .data_av(data_av), .aux_four(bloco_dados_1_aux_four), .text_gt(bloco_dados_1_textsize_gt), .rst(rst),
    .clk(clk), .current_state(Current_State), .init(bloco_controle_1_init), .wrAux(bloco_controle_1_wraux),
    .res_aux(bloco_controle_1_res_aux), .done(done), .Mux1(bloco_controle_1_mux1),
    .Mux2(bloco_controle_1_mux2), .Mux3(bloco_controle_1_mux3), .Mux4(bloco_controle_1_mux4),
    .MuxAux(bloco_controle_1_muxaux), .wrI(bloco_controle_1_wri), .wrJ(bloco_controle_1_wrj),
    .MuxData(bloco_controle_1_muxdata), .wrK(bloco_controle_1_wrk), .rst_IJK(bloco_controle_1_rst_ijk),
    .sel(sel), .ld(ld));
  Bloco_Dados bloco_dados_1 (
    .clock(clk), .reset(rst), .data(data), .init(bloco_controle_1_init), .rst_ijk(bloco_controle_1_rst_ijk),
    .wrI(bloco_controle_1_wri), .wrJ(bloco_controle_1_wrj), .wrK(bloco_controle_1_wrk),
    .MuxData(bloco_controle_1_muxdata), .MuxAux(bloco_controle_1_muxaux), .wrAux(bloco_controle_1_wraux),
    .rst_aux(bloco_controle_1_res_aux), .Mux3(bloco_controle_1_mux3), .Mux4(bloco_controle_1_mux4),
    .Mux1(bloco_controle_1_mux1), .Mux2(bloco_controle_1_mux2), .A(A), .data_in(data_in),
    .data_out(data_out), .aux_four(bloco_dados_1_aux_four), .TextSize_gt(bloco_dados_1_textsize_gt));
endmodule

module prox_estado (
  input  Q2,
  input  Q1,
  input  Q0,
  input  data_av,
  input  k_four,
  input  text_gt,
  output P2,
  output P1,
  output P0
);

  wire and_1_out, and_2_out, and_3_out, and_4_out, and_5_out, and_6_out, and_7_out, and_8_out, and_9_out,
       not_1_out, not_2_out, not_3_out, not_4_out, not_5_out, not_6_out, not_7_out, not_8_out, not_9_out;

  not not_1 (not_1_out, Q0);
  not not_2 (not_2_out, Q1);
  not not_3 (not_3_out, Q2);
  not not_4 (not_4_out, Q2);
  not not_5 (not_5_out, Q1);
  not not_6 (not_6_out, Q1);
  not not_7 (not_7_out, Q0);
  not not_8 (not_8_out, Q1);
  not not_9 (not_9_out, Q1);
  and and_1 (and_1_out, Q1, not_1_out);
  and and_2 (and_2_out, Q2, not_2_out);
  and and_3 (and_3_out, not_3_out, Q0, text_gt);
  and and_4 (and_4_out, not_4_out, Q1);
  and and_5 (and_5_out, Q2, not_5_out, Q0);
  and and_6 (and_6_out, not_6_out, not_7_out, k_four);
  and and_7 (and_7_out, not_8_out, Q0, text_gt);
  and and_8 (and_8_out, Q2, not_9_out);
  and and_9 (and_9_out, Q2, Q0);
  or or_1 (P2, and_1_out, and_2_out);
  or or_2 (P1, and_3_out, and_4_out, and_5_out);
  or or_3 (P0, and_6_out, and_7_out, and_8_out, and_9_out);
endmodule

module saidas_mealy (
  input  Q2,
  input  Q1,
  input  Q0,
  input  data_av,
  input  aux_four,
  input  text_gt,
  output init,
  output wrAux,
  output res_aux,
  output done
);

  wire and_1_out, and_2_out, and_3_out, and_4_out, and_5_out, and_6_out, and_7_out, and_8_out, not_1_out,
       not_2_out, not_3_out, not_4_out, not_5_out, not_6_out, not_7_out, not_8_out, not_9_out, not_10_out,
       not_11_out, not_12_out, not_13_out, not_14_out, not_15_out;

  not not_1 (not_1_out, Q2);
  not not_2 (not_2_out, Q1);
  not not_3 (not_3_out, Q0);
  not not_4 (not_4_out, aux_four);
  not not_5 (not_5_out, Q2);
  not not_6 (not_6_out, Q1);
  not not_7 (not_7_out, text_gt);
  not not_8 (not_8_out, Q2);
  not not_9 (not_9_out, aux_four);
  not not_10 (not_10_out, Q2);
  not not_11 (not_11_out, Q2);
  not not_12 (not_12_out, Q2);
  not not_13 (not_13_out, Q2);
  not not_14 (not_14_out, Q1);
  not not_15 (not_15_out, text_gt);
  and and_1 (and_1_out, not_1_out, not_2_out, not_3_out, data_av, not_4_out);
  and and_2 (and_2_out, not_5_out, not_6_out, Q0, not_7_out);
  and and_3 (and_3_out, not_8_out, data_av, not_9_out);
  and and_4 (and_4_out, not_10_out, Q0);
  and and_5 (and_5_out, not_11_out, Q1);
  and and_6 (and_6_out, Q1, Q0);
  and and_7 (and_7_out, not_12_out, Q0);
  and and_8 (and_8_out, Q1, Q0);
  and and_9 (done, not_13_out, not_14_out, Q0, not_15_out);
  or or_1 (init, and_1_out, and_2_out);
  or or_2 (wrAux, and_3_out, and_4_out, and_5_out, and_6_out);
  or or_3 (res_aux, and_7_out, and_8_out);
endmodule

module saidas_moore_2 (
  input  Q2,
  input  Q1,
  input  Q0,
  output rst_IJK,
  output sel,
  output ld
);

  wire and_2_out, not_1_out, not_2_out, not_3_out, not_4_out, not_5_out;

  not not_1 (not_1_out, Q2);
  not not_2 (not_2_out, Q1);
  not not_3 (not_3_out, Q0);
  not not_4 (not_4_out, Q1);
  and and_1 (rst_IJK, not_1_out, not_2_out, not_3_out);
  not not_5 (not_5_out, Q2);
  and and_2 (and_2_out, not_4_out, Q0);
  or or_1 (ld, not_5_out, and_2_out);

  assign sel = 1'b1;
endmodule

module saidas_moore (
  input  Q2,
  input  Q1,
  input  Q0,
  output Mux1,
  output Mux2_1,
  output Mux2_0,
  output Mux3_1,
  output Mux3_0,
  output Mux4_1,
  output Mux4_0,
  output MuxAux,
  output wrI,
  output wrJ,
  output MuxData,
  output wrK
);

  wire and_1_out, and_2_out, and_3_out, and_4_out, and_5_out, and_6_out, and_7_out, and_8_out, and_9_out,
       and_10_out, and_11_out, and_12_out, and_13_out, and_14_out, and_15_out, and_16_out, and_18_out,
       and_19_out, not_1_out, not_2_out, not_3_out, not_4_out, not_5_out, not_6_out, not_7_out, not_8_out,
       not_9_out, not_10_out, not_11_out, not_12_out, not_13_out, not_14_out, not_15_out, not_16_out,
       not_17_out, not_18_out, not_19_out, not_20_out, not_21_out, not_22_out, not_23_out, not_24_out,
       not_25_out, not_26_out, not_27_out, not_28_out, not_29_out, not_30_out;

  not not_1 (not_1_out, Q2);
  not not_2 (not_2_out, Q1);
  not not_3 (not_3_out, Q1);
  not not_4 (not_4_out, Q0);
  not not_5 (not_5_out, Q2);
  not not_6 (not_6_out, Q1);
  not not_7 (not_7_out, Q0);
  not not_8 (not_8_out, Q2);
  not not_9 (not_9_out, Q1);
  not not_10 (not_10_out, Q0);
  not not_11 (not_11_out, Q1);
  not not_12 (not_12_out, Q0);
  not not_13 (not_13_out, Q1);
  not not_14 (not_14_out, Q1);
  not not_15 (not_15_out, Q0);
  not not_16 (not_16_out, Q0);
  not not_17 (not_17_out, Q1);
  not not_18 (not_18_out, Q2);
  not not_19 (not_19_out, Q1);
  not not_20 (not_20_out, Q0);
  not not_21 (not_21_out, Q2);
  not not_22 (not_22_out, Q2);
  not not_23 (not_23_out, Q0);
  not not_24 (not_24_out, Q2);
  not not_25 (not_25_out, Q1);
  not not_26 (not_26_out, Q2);
  not not_27 (not_27_out, Q1);
  not not_28 (not_28_out, Q0);
  and and_1 (and_1_out, not_1_out, not_2_out);
  and and_2 (and_2_out, Q2, Q1, Q0);
  not not_29 (not_29_out, Q2);
  and and_3 (and_3_out, not_3_out, Q0);
  and and_4 (and_4_out, Q1, not_4_out);
  or or_1 (Mux2_0, not_5_out, Q0);
  and and_5 (and_5_out, not_6_out, not_7_out);
  and and_6 (and_6_out, not_8_out, Q1, Q0);
  and and_7 (and_7_out, Q2, not_9_out);
  and and_8 (and_8_out, Q2, not_10_out);
  not not_30 (not_30_out, Q0);
  and and_9 (and_9_out, Q2, not_11_out);
  and and_10 (and_10_out, Q1, not_12_out);
  and and_11 (and_11_out, Q2, not_13_out);
  and and_12 (and_12_out, not_14_out, not_15_out);
  and and_13 (and_13_out, Q1, Q0);
  and and_14 (and_14_out, Q2, not_16_out);
  or or_2 (MuxAux, not_17_out, Q2);
  and and_15 (and_15_out, not_18_out, not_19_out, not_20_out);
  and and_16 (and_16_out, not_21_out, Q1, Q0);
  and and_17 (wrJ, not_22_out, not_23_out);
  or or_3 (MuxData, not_24_out, not_25_out);
  and and_18 (and_18_out, not_26_out, not_27_out, not_28_out);
  and and_19 (and_19_out, Q2, Q1, Q0);
  or or_4 (Mux1, and_1_out, and_2_out);
  or or_5 (Mux2_1, not_29_out, and_3_out, and_4_out);
  or or_6 (Mux3_1, and_5_out, and_6_out, and_7_out, and_8_out);
  or or_7 (Mux3_0, not_30_out, and_9_out);
  or or_8 (Mux4_1, and_10_out, and_11_out);
  or or_9 (Mux4_0, and_12_out, and_13_out, and_14_out);
  or or_10 (wrI, and_15_out, and_16_out);
  or or_11 (wrK, and_18_out, and_19_out);
endmodule

// sinc
module button_sinc (
  input  bt_in,
  input  clock,
  input  reset,
  output bt_out
);

  wire and_1_out, d_ff_1_q, d_ff_2_qn;

  and and_1 (and_1_out, bt_in, d_ff_1_q);
  D_Flip_Flop d_ff_1 (.clk(clock), .D(bt_in), .Q(d_ff_1_q), .reset(reset));  // open: Qn, preset, en
  D_Flip_Flop d_ff_2 (.clk(clock), .D(and_1_out), .Qn(d_ff_2_qn), .reset(reset));  // open: Q, preset, en
  and and_2 (bt_out, d_ff_1_q, d_ff_2_qn);
endmodule

module COMPLETO (
  input  [7:0] data,
  output done
);

  wire and_1_out, and_2_out, bloco_controle_1_init, bloco_controle_1_ld, bloco_controle_1_mux1,
       bloco_controle_1_muxaux, bloco_controle_1_muxdata, bloco_controle_1_res_aux, bloco_controle_1_rst_ijk,
       bloco_controle_1_sel, bloco_controle_1_wraux, bloco_controle_1_wri, bloco_controle_1_wrj,
       bloco_controle_1_wrk, button_sinc_1_bt_out, clk, data_av_out, not_2_out, or_1_out, or_2_out, rst;
  wire [1:0] bloco_controle_1_mux2, bloco_controle_1_mux3, bloco_controle_1_mux4;
  wire [2:0] bloco_controle_1_current_state;
  wire [7:0] adder_1_out, adder_2_out, divider_1_rem, multiplexer_1_out, multiplexer_2_out,
       multiplexer_3_out, multiplexer_4_out, multiplexer_5_out, multiplexer_6_out, not_1_out, ram_1_data,
       RegAux_q, RegI_q, RegJ_q, RegK_q, RegKeyStream_q, RegMEM_q, RegState_q, RegStateSize_q, RegTextSize_q;

  Clock clock (.out(clk));
  Button reset (.out(rst));
  Button data_av (.out(data_av_out));
  // Probe on data
  // Probe on data
  button_sinc button_sinc_1 (.bt_in(data_av_out), .clock(clk), .reset(rst), .bt_out(button_sinc_1_bt_out));
  Multiplexer #(.width(8), .enable("false")) multiplexer_1 (
    .in0(RegMEM_q), .in1(adder_1_out), .out(multiplexer_1_out), .sel(bloco_controle_1_muxaux));
  Register RegI (.D(divider_1_rem), .en(bloco_controle_1_wri), .Q(RegI_q), .clk(clk), .clr(or_1_out));
  Register RegJ (.D(divider_1_rem), .en(bloco_controle_1_wrj), .Q(RegJ_q), .clk(clk), .clr(or_1_out));
  Register RegK (.D(adder_1_out), .en(bloco_controle_1_wrk), .Q(RegK_q), .clk(clk), .clr(or_1_out));
  Register RegAux (.D(multiplexer_1_out), .en(bloco_controle_1_wraux), .Q(RegAux_q), .clk(clk), .clr(or_2_out));
  Register RegKeyStream (.D(data), .en(bloco_controle_1_init), .Q(RegKeyStream_q), .clk(clk), .clr(rst));
  or or_1 (or_1_out, bloco_controle_1_rst_ijk, rst);
  or or_2 (or_2_out, rst, bloco_controle_1_res_aux);
  Register RegTextSize (.D(RegKeyStream_q), .en(bloco_controle_1_init), .Q(RegTextSize_q), .clk(clk), .clr(rst));
  assign not_1_out = ~RegTextSize_q;  // NOT_Gate not_1, 8 bits wide
  Bloco_Controle bloco_controle_1 (
    .data_av(button_sinc_1_bt_out), .aux_four(and_2_out), .text_gt(adder_1_out[7]), .rst(rst), .clk(clk),
    .current_state(bloco_controle_1_current_state), .init(bloco_controle_1_init),
    .wrAux(bloco_controle_1_wraux), .res_aux(bloco_controle_1_res_aux), .done(done),
    .Mux1(bloco_controle_1_mux1), .Mux2(bloco_controle_1_mux2), .Mux3(bloco_controle_1_mux3),
    .Mux4(bloco_controle_1_mux4), .MuxAux(bloco_controle_1_muxaux), .wrI(bloco_controle_1_wri),
    .wrJ(bloco_controle_1_wrj), .MuxData(bloco_controle_1_muxdata), .wrK(bloco_controle_1_wrk),
    .rst_IJK(bloco_controle_1_rst_ijk), .sel(bloco_controle_1_sel), .ld(bloco_controle_1_ld));
  Multiplexer #(.select(2), .width(8), .enable("false")) multiplexer_2 (
    .in0(RegK_q), .in1(RegJ_q), .in2(RegI_q), .in3(RegAux_q), .out(multiplexer_2_out),
    .sel(bloco_controle_1_mux3));
  Multiplexer #(.select(2), .width(8), .enable("false")) multiplexer_3 (
    .in0(not_1_out), .in1(8'h1), .in2(RegMEM_q), .in3({8{1'b0}}), .out(multiplexer_3_out),
    .sel(bloco_controle_1_mux4));
  Register RegStateSize (.D(RegTextSize_q), .en(bloco_controle_1_init), .Q(RegStateSize_q), .clk(clk), .clr(rst));
  and and_1 (and_1_out, ~bloco_controle_1_mux4[0], ~bloco_controle_1_mux4[1]);  // AND_Gate
  // Probe on bloco_controle_1_current_state
  Register RegState (.D(RegStateSize_q), .en(bloco_controle_1_init), .Q(RegState_q), .clk(clk), .clr(rst));
  Divider divider_1 (.a(adder_1_out), .b(RegStateSize_q), .rem(divider_1_rem));  // open: out, upper
  Adder adder_1 (.a(multiplexer_2_out), .b(multiplexer_3_out), .out(adder_1_out), .cin(and_1_out));  // open: cout
  Multiplexer #(.width(8), .enable("false")) multiplexer_4 (
    .in0(RegState_q), .in1(RegKeyStream_q), .out(multiplexer_4_out), .sel(bloco_controle_1_mux1));
  Multiplexer #(.select(2), .width(8), .enable("false")) multiplexer_5 (
    .in0(RegJ_q), .in1(RegK_q), .in2(RegI_q), .in3(divider_1_rem), .out(multiplexer_5_out),
    .sel(bloco_controle_1_mux2));
  Adder adder_2 (.a(multiplexer_4_out), .b(multiplexer_5_out), .out(adder_2_out));  // open: cin, cout
  and and_2 (and_2_out, ~RegAux_q[0], ~RegAux_q[1], RegAux_q[2], ~RegAux_q[3], ~RegAux_q[4], ~RegAux_q[5], ~RegAux_q[6], ~RegAux_q[7]);  // AND_Gate
  Multiplexer #(.width(8), .enable("false")) multiplexer_6 (
    .in0(RegMEM_q), .in1(RegAux_q), .out(multiplexer_6_out), .sel(bloco_controle_1_muxdata));
  RAM ram_1 (
    .addr(adder_2_out), .data(ram_1_data), .sel(bloco_controle_1_sel), .clk(clk), .ld(bloco_controle_1_ld));  // open: clr
  not not_2 (not_2_out, bloco_controle_1_ld);
  Register RegMEM (.D(ram_1_data), .en(bloco_controle_1_ld), .Q(RegMEM_q), .clk(clk), .clr(rst));
  assign ram_1_data = not_2_out ? multiplexer_6_out : 8'bz;  // Controlled_Buffer controlled_buffer_1

  // Notes on the sheet:
  //   init
  //   rst_IJK
  //   wrI
  //   wrJ
  //   wrK
  //   MuxAux
  //   wrAux
  //   res_Aux
  //   Mux3
  //   Mux4
  //   Mux1
  //   Mux2
  //   Aux_Four
  //   text_gt
  //   sel
  //   MuxData
  //   ld
endmodule
